// Logisim project finished - Copy.circ as structural Verilog
module ALU (
  input  [2:0] F,
  input  [31:0] B,
  input  [31:0] A,
  output zero,
  output [31:0] Y
);

  wire bitselector_2_out, nor_1_out, nor_2_out, nor_3_out, nor_4_out, nor_5_out, nor_6_out, nor_7_out,
       nor_8_out;
  wire [7:0] bitselector_1_out;
  wire [31:0] adder_1_out, and_1_out, bit_extender_1_out, multiplexer_1_out, multiplier_1_out, not_1_out,
       or_1_out;

  assign not_1_out = ~B;  // NOT_Gate not_1, 32 bits wide
  Multiplexer #(.width(32), .enable("false")) multiplexer_1 (
    .in0(B), .in1(not_1_out), .out(multiplexer_1_out), .sel(F[2]));
  Multiplier #(.width(32)) multiplier_1 (.a(A), .b(multiplexer_1_out), .out(multiplier_1_out));  // open: cin, cout
  assign and_1_out = multiplexer_1_out & A;  // AND_Gate and_1, 32 bits wide
  assign or_1_out = multiplexer_1_out | A;  // OR_Gate or_1, 32 bits wide
  Adder #(.width(32)) adder_1 (.a(multiplexer_1_out), .b(A), .out(adder_1_out), .cin(F[2]));  // open: cout
  BitSelector #(.width(32), .group(8)) bitselector_1 (.in(adder_1_out), .out(bitselector_1_out), .sel(2'b11));
  BitSelector bitselector_2 (.in(bitselector_1_out), .out(bitselector_2_out), .sel(3'b111));
  Multiplexer #(.select(3), .width(32), .enable("false")) multiplexer_2 (
    .in0(and_1_out), .in1(or_1_out), .in2(adder_1_out), .in3(multiplier_1_out), .in6(adder_1_out),
    .in7(bit_extender_1_out), .out(Y), .sel(F));  // open: in4, in5
  assign bit_extender_1_out = {{31{1'b0}}, bitselector_2_out};  // Bit_Extender bit_extender_1
  nor nor_1 (nor_1_out, Y[8], Y[9], Y[10], Y[11]);
  nor nor_2 (nor_2_out, Y[12], Y[13], Y[14], Y[15]);
  nor nor_3 (nor_3_out, Y[16], Y[17], Y[18], Y[19]);
  nor nor_4 (nor_4_out, Y[20], Y[21], Y[22], Y[23]);
  nor nor_5 (nor_5_out, Y[24], Y[25], Y[26], Y[27]);
  nor nor_6 (nor_6_out, Y[28], Y[29], Y[30], Y[31]);
  nor nor_7 (nor_7_out, Y[0], Y[1], Y[2], Y[3]);
  nor nor_8 (nor_8_out, Y[4], Y[5], Y[6], Y[7]);
  and and_2 (zero, nor_7_out, nor_8_out, nor_1_out, nor_2_out, nor_3_out, nor_4_out, nor_5_out, nor_6_out);
endmodule

module Datapath (
  input  set_PC___0,
  output [31:0] A,
  output [20:0] out_3,
  output [2:0] rs,
  output [31:0] B,
  output [2:0] out_6,
  output [31:0] v0
);

  wire alu_1_zero, and_1_out, clock_1_out, controlunit_1_alusrc, controlunit_1_branch,
       controlunit_1_regwrite, RegDst;
  wire [2:0] bitselector_7_out, controlunit_1_alucontrol, multiplexer_3_out;
  wire [7:0] adder_1_out, adder_2_out, bitselector_1_out, multiplexer_1_out, multiplexer_2_out, register_1_q,
       shifter_1_out;
  wire [10:0] bitselector_3_out;
  wire [15:0] bitselector_2_out, bitselector_8_out;
  wire [31:0] alu_1_y, bit_extender_1_out, multiplexer_4_out, rom_1_data, shifter_2_out;

  Multiplexer #(.width(8), .enable("false")) multiplexer_1 (
    .in0(adder_2_out), .in1(adder_1_out), .out(multiplexer_1_out), .sel(and_1_out));
  Clock clock_1 (.out(clock_1_out));
  Multiplexer #(.width(8), .enable("false")) multiplexer_2 (
    .in0(multiplexer_1_out), .in1({8{1'b0}}), .out(multiplexer_2_out), .sel(set_PC___0));
  Register register_1 (.D(multiplexer_2_out), .Q(register_1_q), .clk(clock_1_out));  // open: en, clr
  Adder adder_1 (.a(adder_2_out), .b(bitselector_1_out), .out(adder_1_out));  // open: cin, cout
  Adder adder_2 (.a(register_1_q), .b(8'h4), .out(adder_2_out));  // open: cin, cout
  Shifter #(.shift("lr")) shifter_1 (.in(register_1_q), .\dist (3'b010), .out(shifter_1_out));
  Shifter #(.width(32)) shifter_2 (.in(bit_extender_1_out), .\dist (5'b00010), .out(shifter_2_out));
  ROM #(.dataWidth(32)) rom_1 (.addr(shifter_1_out), .data(rom_1_data));  // open: sel
  BitSelector #(.width(32), .group(8)) bitselector_1 (.in(shifter_2_out), .out(bitselector_1_out), .sel(2'b00));
  BitSelector #(.width(32), .group(16)) bitselector_2 (.in(rom_1_data), .out(bitselector_2_out), .sel(1'b1));
  BitSelector #(.width(32), .group(11)) bitselector_3 (.in(rom_1_data), .out(bitselector_3_out), .sel(2'b01));
  and and_1 (and_1_out, alu_1_zero, controlunit_1_branch);
  ControlUnit controlunit_1 (
    .RegDst(RegDst), .Instruction(rom_1_data), .RegWrite(controlunit_1_regwrite),
    .ALUSrc(controlunit_1_alusrc), .Branch(controlunit_1_branch), .ALUControl(controlunit_1_alucontrol));
  BitSelector #(.width(21), .group(3)) bitselector_4 (.in(out_3), .out(rs), .sel(3'b000));
  BitSelector #(.width(32), .group(21)) bitselector_5 (.in(rom_1_data), .out(out_3), .sel(1'b1));
  BitSelector #(.width(16), .group(3)) bitselector_6 (.in(bitselector_2_out), .out(out_6), .sel(3'b000));
  BitSelector #(.width(11), .group(3)) bitselector_7 (.in(bitselector_3_out), .out(bitselector_7_out), .sel(2'b00));
  Multiplexer #(.width(3), .enable("false")) multiplexer_3 (
    .in0(out_6), .in1(bitselector_7_out), .out(multiplexer_3_out), .sel(RegDst));
  assign bit_extender_1_out = {{16{bitselector_8_out[15]}}, bitselector_8_out};  // Bit_Extender bit_extender_1
  BitSelector #(.width(32), .group(16)) bitselector_8 (.in(rom_1_data), .out(bitselector_8_out), .sel(1'b0));
  RegisterFile registerfile_1 (
    .CLK(clock_1_out), .A1(rs), .WD3(alu_1_y), .A2(out_6), .WE3(controlunit_1_regwrite), .RD1(A), .RD2(B),
    .A3(multiplexer_3_out), .V0(v0));  // open: Res
  Multiplexer #(.width(32), .enable("false")) multiplexer_4 (
    .in0(B), .in1(bit_extender_1_out), .out(multiplexer_4_out), .sel(controlunit_1_alusrc));
  ALU alu_1 (.zero(alu_1_zero), .F(controlunit_1_alucontrol), .B(multiplexer_4_out), .Y(alu_1_y), .A(A));

  // Notes on the sheet:
  //   contents of rom_1 (hex, n*v repeats v):
  //   20040004 20030001 10040006 42820 33020 70a61002 401820 2084ffff 1000fff9 601020 0 1000fffe
endmodule

module Tests (
  output [31:0] Y,
  output [11:0] out_2,
  output [7:0] out_3,
  output [2:0] out_4
);

  BitSelector #(.width(32), .group(12)) bitselector_1 (.in(32'h12356789), .out(out_2), .sel(2'b00));
  BitSelector #(.width(32), .group(8)) bitselector_2 (.in(32'h12356789), .out(out_3), .sel(2'b01));
  BitSelector #(.group(3)) bitselector_3 (.in(out_3), .out(out_4), .sel(2'b00));

  assign Y = 32'hf4010207;

  // Notes on the sheet:
  //   binary values in Logisim. Convince yourself how the bits are displayed.
  //   Example 2: The bit selector is configured to have 32  
  //   bit group #1 (starting at index 0) is selected for the output.
  //   That is, the 8 bits 0x67 at bit indices 15..8  are sent to the output.
  //   Example 3: Now, assume that you want to extract 3 bits at   
  //   Example 1: A simple example that illustrates how 32-bit values are displayed as 
  //   input bits and 8 output bits. The parameter constant is 1, which means that   
  //   bit indices 10..8. This can be accoplished by putting two bit selecotrs in series.
endmodule

module RegisterFile (
  input  CLK,
  input  [2:0] A1,
  input  [31:0] WD3,
  input  [2:0] A2,
  input  WE3,
  input  [2:0] A3,
  input  Res,
  output [31:0] RD1,
  output [31:0] RD2,
  output [31:0] V0
);

  wire and_1_out, and_2_out, and_3_out, and_4_out, and_5_out, and_6_out, and_7_out, decoder_1_out1,
       decoder_1_out2, decoder_1_out3, decoder_1_out4, decoder_1_out5, decoder_1_out6, decoder_1_out7;
  wire [31:0] register_1_q, register_3_q, register_4_q, register_5_q, register_6_q, register_7_q;

  Decoder #(.select(3)) decoder_1 (
    .out1(decoder_1_out1), .out2(decoder_1_out2), .out3(decoder_1_out3), .out4(decoder_1_out4),
    .out5(decoder_1_out5), .out6(decoder_1_out6), .out7(decoder_1_out7), .sel(A3));  // open: out0, en
  and and_1 (and_1_out, WE3, decoder_1_out1);
  and and_2 (and_2_out, WE3, decoder_1_out2);
  and and_3 (and_3_out, WE3, decoder_1_out3);
  and and_4 (and_4_out, WE3, decoder_1_out4);
  and and_5 (and_5_out, WE3, decoder_1_out5);
  and and_6 (and_6_out, WE3, decoder_1_out6);
  and and_7 (and_7_out, WE3, decoder_1_out7);
  Register #(.width(32)) register_1 (.D(WD3), .en(and_1_out), .Q(register_1_q), .clk(CLK), .clr(Res));
  Register #(.width(32)) register_2 (.D(WD3), .en(and_2_out), .Q(V0), .clk(CLK), .clr(Res));
  Register #(.width(32)) register_3 (.D(WD3), .en(and_3_out), .Q(register_3_q), .clk(CLK), .clr(Res));
  Register #(.width(32)) register_4 (.D(WD3), .en(and_4_out), .Q(register_4_q), .clk(CLK), .clr(Res));
  Register #(.width(32)) register_5 (.D(WD3), .en(and_5_out), .Q(register_5_q), .clk(CLK), .clr(Res));
  Register #(.width(32)) register_6 (.D(WD3), .en(and_6_out), .Q(register_6_q), .clk(CLK), .clr(Res));
  Register #(.width(32)) register_7 (.D(WD3), .en(and_7_out), .Q(register_7_q), .clk(CLK), .clr(Res));
  Multiplexer #(.select(3), .width(32)) multiplexer_1 (
    .in0({32{1'b0}}), .in1(register_1_q), .in2(V0), .in3(register_3_q), .in4(register_4_q),
    .in5(register_5_q), .in6(register_6_q), .in7(register_7_q), .out(RD1), .sel(A1));  // open: en
  Multiplexer #(.select(3), .width(32)) multiplexer_2 (
    .in0({32{1'b0}}), .in1(register_1_q), .in2(V0), .in3(register_3_q), .in4(register_4_q),
    .in5(register_5_q), .in6(register_6_q), .in7(register_7_q), .out(RD2), .sel(A2));  // open: en
endmodule

module ControlUnit (
  input  [31:0] Instruction,
  output RegDst,
  output RegWrite,
  output ALUSrc,
  output Branch,
  output [2:0] ALUControl
);

  wire and_1_out, comparator_2_eq, comparator_4_eq, not_1_out, not_2_out;
  wire [2:0] multiplexer_1_out;
  wire [5:0] bitselector_1_out;
  wire [31:0] shifter_1_out;

  Shifter #(.width(32), .shift("lr")) shifter_1 (.in(Instruction), .\dist (5'b11010), .out(shifter_1_out));
  BitSelector #(.width(32), .group(6)) bitselector_1 (.in(shifter_1_out), .out(bitselector_1_out), .sel(3'b000));
  Comparator #(.width(6), .mode("unsigned")) comparator_1 (
    .a(bitselector_1_out), .b(6'b001000), .eq(ALUSrc));  // open: gt, lt
  Comparator #(.width(6), .mode("unsigned")) comparator_2 (
    .a(bitselector_1_out), .b({6{1'b0}}), .eq(comparator_2_eq));  // open: gt, lt
  Comparator #(.width(6), .mode("unsigned")) comparator_3 (
    .a(bitselector_1_out), .b(6'b000100), .eq(Branch));  // open: gt, lt
  Comparator #(.width(6), .mode("unsigned")) comparator_4 (
    .a(bitselector_1_out), .b(6'b011100), .eq(comparator_4_eq));  // open: gt, lt
  or or_1 (RegWrite, ALUSrc, comparator_4_eq, comparator_2_eq);
  not not_1 (not_1_out, ALUSrc);
  not not_2 (not_2_out, comparator_2_eq);
  or or_2 (RegDst, comparator_4_eq, comparator_2_eq);
  and and_1 (and_1_out, not_1_out, not_2_out, Branch);
  Multiplexer #(.width(3), .enable("false")) multiplexer_1 (
    .in0(3'b010), .in1(3'b110), .out(multiplexer_1_out), .sel(and_1_out));
  Multiplexer #(.width(3), .enable("false")) multiplexer_2 (
    .in0(multiplexer_1_out), .in1(3'b011), .out(ALUControl), .sel(comparator_4_eq));

  // Notes on the sheet:
  //   get op code
  //   get 6 LSB
  //   if ==0, add
  //   if ==28, mult
  //   if ==8, addi
endmodule
